# Fritzing sketch EuglenaArcade (saved by Fritzing 0.9.2b)
breadboards: 1

parts:
  R1 = Resistor [tolerance=±5% resistance=220 package=THT]
  R2 = Resistor [tolerance=±5% resistance=220 package=THT]
  LED1 = LED - 5mm [color="White (4500K)" package="5 mm [THT]"]
  LED2 = LED - 5mm [color="White (4500K)" package="5 mm [THT]"]
  LED3 = LED - 5mm [color="White (4500K)" package="5 mm [THT]"]
  LED4 = LED - 5mm [color="White (4500K)" package="5 mm [THT]"]
  U1 = mystery part, 9 pins [chip_label="PS2 Controller Connector"]
  Part1 = Arduino Nano (Rev3.0) (ICSP)

nets:
  N1: R1.Pin_0, LED1.cathode, LED2.cathode
  GND: R1.Pin_1, R2.Pin_0, U1.pin4, Part1.GND
  N2: R2.Pin_1, LED3.cathode, LED4.cathode
  N3: LED1.anode, Part1.D3
  N4: LED2.anode, Part1.D5
  N5: LED3.anode, Part1.D6
  N6: LED4.anode, Part1.D9
  N7: U1.pin1, Part1.D12/MISO
  N8: U1.pin2, Part1.D11/MOSI
  N9: U1.pin5, Part1.3V3
  N10: U1.pin6, Part1.D10
  N11: U1.pin7, Part1.D13/SCK
